// Logisim project N-1.circ as structural Verilog: 5 circuits, main circuit Simple_PC
module NEUTROSER_N1 (
  input  CLK,
  input  RST,
  input  DI0,
  input  DI1,
  input  DI2,
  input  DI3,
  input  DI4,
  input  DI5,
  input  DI6,
  input  DI7,
  input  DI8,
  input  DI9,
  input  DI10,
  input  DI11,
  input  DI12,
  input  DI13,
  input  DI14,
  input  DI15,
  output WE,
  output MC0,
  output MC1,
  output MC2,
  output SYNC,
  output MC3,
  output MC4,
  output MC5,
  output MC6,
  output MC7,
  output DO0,
  output DO1,
  output DO2,
  output DO3,
  output DO4,
  output DO5,
  output DO6,
  output DO7,
  output DO8,
  output DO9,
  output DO10,
  output DO11,
  output DO12,
  output DO13,
  output DO14,
  output DO15
);

  wire and_1_out, and_4_out, and_5_out, and_6_out, and_7_out, and_8_out, and_9_out, and_10_out, and_11_out,
       and_12_out, and_13_out, and_14_out, and_15_out, CEND, CHANGE, cmdclk, counter_2_q, cswitch, DIV, INV,
       JUMP, LAND, LOAD, LOR, LXOR, MUL, not_1_out, not_2_out, not_3_out, or_2_out, SHL, SHR, SUB, SUM, WRITE;
  wire [4:0] bit_extender_1_out;
  wire [7:0] ADDR, counter_1_q, register_3_q;
  wire [15:0] multiplexer_2_out, nealu_1_lout, PRAM;

  not not_1 (not_1_out, JUMP);
  Counter #(.ongoal("stay"), .trigger("falling")) counter_1 (
    .load(JUMP), .D({DI7, DI6, DI5, DI4, DI3, DI2, DI1, DI0}), .count(not_1_out), .Q(counter_1_q),
    .clk(and_1_out), .clr(RST));  // open: carry, up
  and and_1 (and_1_out, cswitch, not_2_out);
  or or_1 (SYNC, CLK, RST);
  not not_2 (not_2_out, counter_2_q);
  Counter #(.max('h1), .ongoal("stay"), .width(1)) counter_2 (
    .Q(counter_2_q), .clk(CEND), .clr(RST));  // open: load, D, count, carry, up
  Multiplexer #(.width(8)) multiplexer_1 (
    .in0(counter_1_q), .in1(ADDR), .out({MC7, MC6, MC5, MC4, MC3, MC2, MC1, MC0}), .sel(cswitch));
  and and_2 (WE, cswitch, WRITE);
  Counter #(.max('h1), .width(1)) counter_3 (.Q(cswitch), .clk(CLK), .clr(RST));  // open: load, D, count, carry, up
  Register #(.trigger("falling"), .width(16)) register_1 (
    .D({DI15, DI14, DI13, DI12, DI11, DI10, DI9, DI8, DI7, DI6, DI5, DI4, DI3, DI2, DI1, DI0}), .Q(PRAM),
    .clk(cswitch), .clr(RST));  // open: en
  Register register_2 (.D({DI7, DI6, DI5, DI4, DI3, DI2, DI1, DI0}), .Q(ADDR), .clk(cswitch), .clr(RST));  // open: en
  Register register_3 (
    .D({DI15, DI14, DI13, DI12, DI11, DI10, DI9, DI8}), .Q(register_3_q), .clk(cswitch), .clr(RST));  // open: en
  Decoder #(.select(5)) decoder_1 (
    .out1(LOAD), .out2(JUMP), .out3(SUM), .out4(SUB), .out5(MUL), .out6(DIV), .out7(INV), .out8(LAND),
    .out9(LOR), .out10(LXOR), .out11(WRITE), .out12(CHANGE), .out13(SHR), .out14(SHL), .out15(CEND),
    .sel(bit_extender_1_out));  // open: out0, out16, out17, out18, out19, out20, out21, out22, out23, out24, out25, out26, out27, out28, out29, out30, out31, en
  Bit_Extender #(.out_width(5)) bit_extender_1 (.in(register_3_q), .out(bit_extender_1_out));
  not not_3 (not_3_out, cswitch);
  and and_3 (cmdclk, not_3_out, CLK);
  NeALU nealu_1 (
    .LOUT(nealu_1_lout), .MUL(MUL), .LAND(LAND), .LOR(LOR), .LXOR(LXOR), .DIV(DIV), .INV(INV), .SHR(SHR),
    .SHL(SHL), .SUM(SUM), .SUB(SUB), .B(PRAM),
    .A({DO15, DO14, DO13, DO12, DO11, DO10, DO9, DO8, DO7, DO6, DO5, DO4, DO3, DO2, DO1, DO0}));
  and and_4 (and_4_out, SHL, cmdclk);
  and and_5 (and_5_out, SHR, cmdclk);
  and and_6 (and_6_out, INV, cmdclk);
  and and_7 (and_7_out, DIV, cmdclk);
  and and_8 (and_8_out, MUL, cmdclk);
  and and_9 (and_9_out, SUB, cmdclk);
  and and_10 (and_10_out, SUM, cmdclk);
  and and_11 (and_11_out, LAND, cmdclk);
  and and_12 (and_12_out, LOR, cmdclk);
  and and_13 (and_13_out, LXOR, cmdclk);
  and and_14 (and_14_out, LOAD, cmdclk);
  Multiplexer #(.width(16)) multiplexer_2 (.in0(nealu_1_lout), .in1(PRAM), .out(multiplexer_2_out), .sel(LOAD));
  or or_2 (or_2_out, and_4_out, and_5_out, and_6_out, and_7_out, and_8_out, and_9_out, and_10_out, and_11_out, and_12_out, and_13_out, and_14_out);
  and and_15 (and_15_out, cmdclk, CHANGE);
  NeRegs neregs_1 (
    .ROUT({DO15, DO14, DO13, DO12, DO11, DO10, DO9, DO8, DO7, DO6, DO5, DO4, DO3, DO2, DO1, DO0}),
    .LOCK(not_3_out), .ADDRCLK(and_15_out), .ADDR(PRAM), .RST(RST), .DATA(multiplexer_2_out), .CLK(or_2_out));

  // Other names for the same wires on the sheet: CDDR[7:0] = {DI7, DI6, DI5, DI4, DI3, DI2, DI1, DI0};
  //   PCOUNTER[7:0] = {MC7, MC6, MC5, MC4, MC3, MC2, MC1, MC0}; RCLK = CLK;
  //   regis[15:0] = {DO15, DO14, DO13, DO12, DO11, DO10, DO9, DO8, DO7, DO6, DO5, DO4, DO3, DO2, DO1, DO0}

  // Notes on the sheet:
  //   LOAD 01
  //   JUMP 02
  //   SUM 03
  //   SUB 04
  //   MUL 05
  //   DIV 06
  //   INV 07
  //   AND 08
  //   OR 09
  //   XOR 0a
  //   WRITE 0b
  //   CHANGE 0c
  //   SHR 0d
  //   SHL 0e
endmodule

module NeALU (
  input  [15:0] A,
  input  [15:0] B,
  input  SUM,
  input  SUB,
  input  MUL,
  input  LAND,
  input  LOR,
  input  LXOR,
  input  DIV,
  input  INV,
  input  SHR,
  input  SHL,
  output [15:0] LOUT
);

  wire nor_1_out;
  wire [3:0] bit_extender_1_out, bit_extender_2_out;
  wire [15:0] adder_1_out, and_1_out, divider_1_out, multiplier_1_out, negator_1_out, or_1_out,
       shifter_1_out, shifter_2_out, subtractor_1_out, xor_1_out;

  Bit_Extender #(.in_width(16), .out_width(4)) bit_extender_1 (.in(B), .out(bit_extender_1_out));
  Bit_Extender #(.in_width(16), .out_width(4)) bit_extender_2 (.in(B), .out(bit_extender_2_out));
  assign LOUT = SHR ? shifter_1_out : 16'bz;  // Controlled_Buffer controlled_buffer_1
  Shifter #(.shift("lr"), .width(16)) shifter_1 (.in(A), .\dist (bit_extender_1_out), .out(shifter_1_out));
  assign LOUT = SHL ? shifter_2_out : 16'bz;  // Controlled_Buffer controlled_buffer_2
  Shifter #(.width(16)) shifter_2 (.in(A), .\dist (bit_extender_2_out), .out(shifter_2_out));
  assign LOUT = INV ? negator_1_out : 16'bz;  // Controlled_Buffer controlled_buffer_3
  Negator #(.width(16)) negator_1 (.in(B), .out(negator_1_out));
  assign LOUT = DIV ? divider_1_out : 16'bz;  // Controlled_Buffer controlled_buffer_4
  Divider #(.mode("twosComplement"), .width(16)) divider_1 (.a(A), .b(B), .out(divider_1_out));  // open: upper, rem
  assign LOUT = SUM ? adder_1_out : 16'bz;  // Controlled_Buffer controlled_buffer_5
  Adder #(.width(16)) adder_1 (.a(A), .b(B), .out(adder_1_out));  // open: cin, cout
  assign LOUT = SUB ? subtractor_1_out : 16'bz;  // Controlled_Buffer controlled_buffer_6
  Subtractor #(.width(16)) subtractor_1 (.a(A), .b(B), .out(subtractor_1_out));  // open: bin, bout
  assign LOUT = MUL ? multiplier_1_out : 16'bz;  // Controlled_Buffer controlled_buffer_7
  Multiplier #(.width(16)) multiplier_1 (.a(A), .b(B), .out(multiplier_1_out));  // open: cin, cout
  assign and_1_out = A & B;  // AND_Gate and_1, 16 bits wide
  assign LOUT = LAND ? and_1_out : 16'bz;  // Controlled_Buffer controlled_buffer_8
  assign or_1_out = A | B;  // OR_Gate or_1, 16 bits wide
  assign LOUT = LOR ? or_1_out : 16'bz;  // Controlled_Buffer controlled_buffer_9
  assign xor_1_out = A ^ B;  // XOR_Gate xor_1, 16 bits wide
  assign LOUT = LXOR ? xor_1_out : 16'bz;  // Controlled_Buffer controlled_buffer_10
  assign LOUT = nor_1_out ? B : 16'bz;  // Controlled_Buffer controlled_buffer_11
  nor nor_1 (nor_1_out, LAND, LXOR, LOR, SUB, MUL, SUM, DIV, INV, SHR, SHL);
endmodule

module NeRegs (
  input  [15:0] DATA,
  input  RST,
  input  [15:0] ADDR,
  input  LOCK,
  input  ADDRCLK,
  input  CLK,
  output [15:0] ROUT
);

  wire decoder_1_out0, decoder_1_out1, decoder_1_out2, decoder_1_out3, decoder_1_out4, decoder_1_out5,
       decoder_1_out6, decoder_1_out7, decoder_1_out8, decoder_1_out9, decoder_1_out10, decoder_1_out11,
       decoder_1_out12, decoder_1_out13, decoder_1_out14, decoder_1_out15;
  wire [3:0] bit_extender_1_out;
  wire [15:0] demultiplexer_1_out0, demultiplexer_1_out1, demultiplexer_1_out2, demultiplexer_1_out3,
       demultiplexer_1_out4, demultiplexer_1_out5, demultiplexer_1_out6, demultiplexer_1_out7,
       demultiplexer_1_out8, demultiplexer_1_out9, demultiplexer_1_out10, demultiplexer_1_out11,
       demultiplexer_1_out12, demultiplexer_1_out13, demultiplexer_1_out14, demultiplexer_1_out15,
       register_1_q, register_2_q, register_3_q, register_4_q, register_5_q, register_6_q, register_7_q,
       register_8_q, register_9_q, register_10_q, register_11_q, register_12_q, register_13_q, register_14_q,
       register_15_q, register_16_q, register_17_q;

  Register #(.trigger("falling"), .width(16)) register_1 (
    .D(ADDR), .en(LOCK), .Q(register_1_q), .clk(ADDRCLK), .clr(RST));
  Demultiplexer #(.select(4), .width(16)) demultiplexer_1 (
    .out0(demultiplexer_1_out0), .out1(demultiplexer_1_out1), .out2(demultiplexer_1_out2),
    .out3(demultiplexer_1_out3), .out4(demultiplexer_1_out4), .out5(demultiplexer_1_out5),
    .out6(demultiplexer_1_out6), .out7(demultiplexer_1_out7), .out8(demultiplexer_1_out8),
    .out9(demultiplexer_1_out9), .out10(demultiplexer_1_out10), .out11(demultiplexer_1_out11),
    .out12(demultiplexer_1_out12), .out13(demultiplexer_1_out13), .out14(demultiplexer_1_out14),
    .out15(demultiplexer_1_out15), .in(DATA), .sel(bit_extender_1_out));
  Bit_Extender #(.in_width(16), .out_width(4)) bit_extender_1 (.in(register_1_q), .out(bit_extender_1_out));
  Decoder #(.select(4)) decoder_1 (
    .out0(decoder_1_out0), .out1(decoder_1_out1), .out2(decoder_1_out2), .out3(decoder_1_out3),
    .out4(decoder_1_out4), .out5(decoder_1_out5), .out6(decoder_1_out6), .out7(decoder_1_out7),
    .out8(decoder_1_out8), .out9(decoder_1_out9), .out10(decoder_1_out10), .out11(decoder_1_out11),
    .out12(decoder_1_out12), .out13(decoder_1_out13), .out14(decoder_1_out14), .out15(decoder_1_out15),
    .sel(bit_extender_1_out), .en(CLK));
  Register #(.trigger("falling"), .width(16)) register_2 (
    .D(demultiplexer_1_out0), .en(LOCK), .Q(register_2_q), .clk(decoder_1_out0), .clr(RST));
  Register #(.trigger("falling"), .width(16)) register_3 (
    .D(demultiplexer_1_out1), .en(LOCK), .Q(register_3_q), .clk(decoder_1_out1), .clr(RST));
  Register #(.trigger("falling"), .width(16)) register_4 (
    .D(demultiplexer_1_out2), .en(LOCK), .Q(register_4_q), .clk(decoder_1_out2), .clr(RST));
  Register #(.trigger("falling"), .width(16)) register_5 (
    .D(demultiplexer_1_out3), .en(LOCK), .Q(register_5_q), .clk(decoder_1_out3), .clr(RST));
  Register #(.trigger("falling"), .width(16)) register_6 (
    .D(demultiplexer_1_out4), .en(LOCK), .Q(register_6_q), .clk(decoder_1_out4), .clr(RST));
  Register #(.trigger("falling"), .width(16)) register_7 (
    .D(demultiplexer_1_out5), .en(LOCK), .Q(register_7_q), .clk(decoder_1_out5), .clr(RST));
  Register #(.trigger("falling"), .width(16)) register_8 (
    .D(demultiplexer_1_out6), .en(LOCK), .Q(register_8_q), .clk(decoder_1_out6), .clr(RST));
  Register #(.trigger("falling"), .width(16)) register_9 (
    .D(demultiplexer_1_out7), .en(LOCK), .Q(register_9_q), .clk(decoder_1_out7), .clr(RST));
  Register #(.trigger("falling"), .width(16)) register_10 (
    .D(demultiplexer_1_out8), .en(LOCK), .Q(register_10_q), .clk(decoder_1_out8), .clr(RST));
  Register #(.trigger("falling"), .width(16)) register_11 (
    .D(demultiplexer_1_out9), .en(LOCK), .Q(register_11_q), .clk(decoder_1_out9), .clr(RST));
  Register #(.trigger("falling"), .width(16)) register_12 (
    .D(demultiplexer_1_out10), .en(LOCK), .Q(register_12_q), .clk(decoder_1_out10), .clr(RST));
  Register #(.trigger("falling"), .width(16)) register_13 (
    .D(demultiplexer_1_out11), .en(LOCK), .Q(register_13_q), .clk(decoder_1_out11), .clr(RST));
  Register #(.trigger("falling"), .width(16)) register_14 (
    .D(demultiplexer_1_out12), .en(LOCK), .Q(register_14_q), .clk(decoder_1_out12), .clr(RST));
  Register #(.trigger("falling"), .width(16)) register_15 (
    .D(demultiplexer_1_out13), .en(LOCK), .Q(register_15_q), .clk(decoder_1_out13), .clr(RST));
  Register #(.trigger("falling"), .width(16)) register_16 (
    .D(demultiplexer_1_out14), .en(LOCK), .Q(register_16_q), .clk(decoder_1_out14), .clr(RST));
  Register #(.trigger("falling"), .width(16)) register_17 (
    .D(demultiplexer_1_out15), .en(LOCK), .Q(register_17_q), .clk(decoder_1_out15), .clr(RST));
  Multiplexer #(.select(4), .width(16)) multiplexer_1 (
    .in0(register_2_q), .in1(register_3_q), .in2(register_4_q), .in3(register_5_q), .in4(register_6_q),
    .in5(register_7_q), .in6(register_8_q), .in7(register_9_q), .in8(register_10_q), .in9(register_11_q),
    .in10(register_12_q), .in11(register_13_q), .in12(register_14_q), .in13(register_15_q),
    .in14(register_16_q), .in15(register_17_q), .out(ROUT), .sel(bit_extender_1_out));
endmodule

module Simple_PC (
);

  wire and_2_out, button_1_out, CLK, clock_1_out, controlled_buffer_2_out, CSYNC, dipswitch_1_sw1, LWE,
       neutroser_n1_1_sync, neutroser_n1_1_we, not_1_out, not_2_out, not_3_out, not_4_out, not_5_out,
       ram_loader_1_sync, RST, RSTProc, rsync, st0, stsy, TRST;
  wire [1:0] counter_1_q;
  wire [6:0] bit_extender_1_out;
  wire [7:0] controlled_buffer_1_out, MC, ram_loader_1_mc;
  wire [15:0] controlled_buffer_6_out, DI, ram_loader_1_dout, rom_1_data, ROUT, shift_register_1_q0,
       shift_register_1_q1, shift_register_1_q2, shift_register_1_q3, shift_register_1_q4,
       shift_register_1_q5, shift_register_1_q6, shift_register_1_q7, shift_register_1_q8,
       shift_register_1_q9, shift_register_1_q10, shift_register_1_q11, shift_register_1_q12,
       shift_register_1_q13, shift_register_1_q14, shift_register_1_q15, shift_register_1_q16,
       shift_register_1_q17, shift_register_1_q18, shift_register_1_q19, shift_register_1_q20,
       shift_register_1_q21, shift_register_1_q22, shift_register_1_q23, shift_register_1_q24,
       shift_register_1_q25, shift_register_1_q26, shift_register_1_q27, shift_register_1_q28,
       shift_register_1_q29, shift_register_1_q30, shift_register_1_q31, shift_register_1_q32,
       shift_register_1_q33, shift_register_1_q34, shift_register_1_q35, shift_register_1_q36,
       shift_register_1_q37, shift_register_1_q38, shift_register_1_q39, shift_register_1_q40,
       shift_register_1_q41, shift_register_1_q42, shift_register_1_q43, shift_register_1_q44,
       shift_register_1_q45, shift_register_1_q46, shift_register_1_q47, shift_register_1_q48,
       shift_register_1_q49, shift_register_1_q50, shift_register_1_q51, shift_register_1_q52,
       shift_register_1_q53, shift_register_1_q54, shift_register_1_q55, shift_register_1_q56,
       shift_register_1_q57, shift_register_1_q58, shift_register_1_q59, shift_register_1_q60,
       shift_register_1_q61, shift_register_1_q62;

  Counter #(.max('h2), .ongoal("stay"), .width(2)) counter_1 (
    .Q(counter_1_q), .clk(st0), .clr(RST));  // open: load, D, count, carry, up
  not not_1 (not_1_out, LWE);
  and and_1 (st0, CLK, not_1_out);
  Counter #(.max('h1), .width(1)) counter_2 (.Q(CSYNC), .clk(stsy), .clr(TRST));  // open: load, D, count, carry, up
  and and_2 (and_2_out, CLK, counter_1_q[1]);
  or or_1 (rsync, st0, stsy);
  or or_2 (TRST, RST, RSTProc);
  ROM #(.dataWidth(16)) rom_1 (.addr(ram_loader_1_mc), .data(rom_1_data));
  not not_2 (not_2_out, LWE);
  assign controlled_buffer_1_out = not_2_out ? MC : 8'bz;  // Controlled_Buffer controlled_buffer_1
  assign controlled_buffer_2_out = not_3_out ? neutroser_n1_1_we : 1'bz;  // Controlled_Buffer controlled_buffer_2
  not not_3 (not_3_out, LWE);
  NEUTROSER_N1 neutroser_n1_1 (
    .SYNC(neutroser_n1_1_sync), .WE(neutroser_n1_1_we), .DO8(ROUT[8]), .DO9(ROUT[9]), .DO10(ROUT[10]),
    .DO11(ROUT[11]), .DO12(ROUT[12]), .DO13(ROUT[13]), .DO14(ROUT[14]), .DO15(ROUT[15]), .DO0(ROUT[0]),
    .DO1(ROUT[1]), .DO2(ROUT[2]), .DO3(ROUT[3]), .DO4(ROUT[4]), .DO5(ROUT[5]), .DO6(ROUT[6]), .DO7(ROUT[7]),
    .MC0(MC[0]), .MC1(MC[1]), .MC2(MC[2]), .MC3(MC[3]), .MC4(MC[4]), .MC5(MC[5]), .MC6(MC[6]), .MC7(MC[7]),
    .CLK(and_2_out), .RST(TRST), .DI10(DI[10]), .DI11(DI[11]), .DI12(DI[12]), .DI13(DI[13]), .DI14(DI[14]),
    .DI15(DI[15]), .DI0(DI[0]), .DI1(DI[1]), .DI2(DI[2]), .DI3(DI[3]), .DI4(DI[4]), .DI5(DI[5]), .DI6(DI[6]),
    .DI7(DI[7]), .DI8(DI[8]), .DI9(DI[9]));
  not not_4 (not_4_out, LWE);
  Button button_1 (.out(button_1_out));
  Clock clock_1 (.out(clock_1_out));
  Button button_2 (.out(RST));
  Button button_3 (.out(RSTProc));
  assign controlled_buffer_2_out = LWE ? LWE : 1'bz;  // Controlled_Buffer controlled_buffer_3
  assign stsy = not_4_out ? neutroser_n1_1_sync : 1'bz;  // Controlled_Buffer controlled_buffer_4
  assign stsy = LWE ? ram_loader_1_sync : 1'bz;  // Controlled_Buffer controlled_buffer_5
  assign controlled_buffer_6_out = not_5_out ? ROUT : 16'bz;  // Controlled_Buffer controlled_buffer_6
  // Probe on ROUT
  or or_3 (CLK, button_1_out, clock_1_out);
  // Probe on controlled_buffer_1_out
  assign controlled_buffer_1_out = LWE ? ram_loader_1_mc : 8'bz;  // Controlled_Buffer controlled_buffer_7
  RAM #(.dataWidth(16), .trigger("falling")) ram_1 (
    .addr(controlled_buffer_1_out), .we(controlled_buffer_2_out), .clk(rsync), .din(controlled_buffer_6_out),
    .dout(DI));  // open: oe
  DipSwitch #(.number(2)) dipswitch_1 (.sw1(dipswitch_1_sw1));  // open: sw2
  RAM_Loader ram_loader_1 (
    .DROM(rom_1_data), .CLK(CLK), .RST(RST), .OnNull(dipswitch_1_sw1), .MC(ram_loader_1_mc),
    .DOUT(ram_loader_1_dout), .SYNC(ram_loader_1_sync), .WE(LWE));
  not not_5 (not_5_out, LWE);
  assign controlled_buffer_6_out = LWE ? ram_loader_1_dout : 16'bz;  // Controlled_Buffer controlled_buffer_8
  // Probe on DI
  Shift_Register #(.length(64), .trigger("falling"), .width(16)) shift_register_1 (
    .in(ROUT), .clk(CSYNC), .clr(TRST), .q0(shift_register_1_q0), .q1(shift_register_1_q1),
    .q2(shift_register_1_q2), .q3(shift_register_1_q3), .q4(shift_register_1_q4), .q5(shift_register_1_q5),
    .q6(shift_register_1_q6), .q7(shift_register_1_q7), .q8(shift_register_1_q8), .q9(shift_register_1_q9),
    .q10(shift_register_1_q10), .q11(shift_register_1_q11), .q12(shift_register_1_q12),
    .q13(shift_register_1_q13), .q14(shift_register_1_q14), .q15(shift_register_1_q15),
    .q16(shift_register_1_q16), .q17(shift_register_1_q17), .q18(shift_register_1_q18),
    .q19(shift_register_1_q19), .q20(shift_register_1_q20), .q21(shift_register_1_q21),
    .q22(shift_register_1_q22), .q23(shift_register_1_q23), .q24(shift_register_1_q24),
    .q25(shift_register_1_q25), .q26(shift_register_1_q26), .q27(shift_register_1_q27),
    .q28(shift_register_1_q28), .q29(shift_register_1_q29), .q30(shift_register_1_q30),
    .q31(shift_register_1_q31), .q32(shift_register_1_q32), .q33(shift_register_1_q33),
    .q34(shift_register_1_q34), .q35(shift_register_1_q35), .q36(shift_register_1_q36),
    .q37(shift_register_1_q37), .q38(shift_register_1_q38), .q39(shift_register_1_q39),
    .q40(shift_register_1_q40), .q41(shift_register_1_q41), .q42(shift_register_1_q42),
    .q43(shift_register_1_q43), .q44(shift_register_1_q44), .q45(shift_register_1_q45),
    .q46(shift_register_1_q46), .q47(shift_register_1_q47), .q48(shift_register_1_q48),
    .q49(shift_register_1_q49), .q50(shift_register_1_q50), .q51(shift_register_1_q51),
    .q52(shift_register_1_q52), .q53(shift_register_1_q53), .q54(shift_register_1_q54),
    .q55(shift_register_1_q55), .q56(shift_register_1_q56), .q57(shift_register_1_q57),
    .q58(shift_register_1_q58), .q59(shift_register_1_q59), .q60(shift_register_1_q60),
    .q61(shift_register_1_q61), .q62(shift_register_1_q62));  // open: shift, out, load, d0, d1, d2, d3, d4, d5, d6, d7, d8, d9, d10, d11, d12, d13, d14, d15, d16, d17, d18, d19, d20, d21, d22, d23, d24, d25, d26, d27, d28, d29, d30, d31, d32, d33, d34, d35, d36, d37, d38, d39, d40, d41, d42, d43, d44, d45, d46, d47, d48, d49, d50, d51, d52, d53, d54, d55, d56, d57, d58, d59, d60, d61, d62, d63, q63
  DotMatrix #(.matrixcols(63), .matrixrows(16)) dotmatrix_1 (
    .col0(shift_register_1_q0), .col1(shift_register_1_q1), .col2(shift_register_1_q2),
    .col3(shift_register_1_q3), .col4(shift_register_1_q4), .col5(shift_register_1_q5),
    .col6(shift_register_1_q6), .col7(shift_register_1_q7), .col8(shift_register_1_q8),
    .col9(shift_register_1_q9), .col10(shift_register_1_q10), .col11(shift_register_1_q11),
    .col12(shift_register_1_q12), .col13(shift_register_1_q13), .col14(shift_register_1_q14),
    .col15(shift_register_1_q15), .col16(shift_register_1_q16), .col17(shift_register_1_q17),
    .col18(shift_register_1_q18), .col19(shift_register_1_q19), .col20(shift_register_1_q20),
    .col21(shift_register_1_q21), .col22(shift_register_1_q22), .col23(shift_register_1_q23),
    .col24(shift_register_1_q24), .col25(shift_register_1_q25), .col26(shift_register_1_q26),
    .col27(shift_register_1_q27), .col28(shift_register_1_q28), .col29(shift_register_1_q29),
    .col30(shift_register_1_q30), .col31(shift_register_1_q31), .col32(shift_register_1_q32),
    .col33(shift_register_1_q33), .col34(shift_register_1_q34), .col35(shift_register_1_q35),
    .col36(shift_register_1_q36), .col37(shift_register_1_q37), .col38(shift_register_1_q38),
    .col39(shift_register_1_q39), .col40(shift_register_1_q40), .col41(shift_register_1_q41),
    .col42(shift_register_1_q42), .col43(shift_register_1_q43), .col44(shift_register_1_q44),
    .col45(shift_register_1_q45), .col46(shift_register_1_q46), .col47(shift_register_1_q47),
    .col48(shift_register_1_q48), .col49(shift_register_1_q49), .col50(shift_register_1_q50),
    .col51(shift_register_1_q51), .col52(shift_register_1_q52), .col53(shift_register_1_q53),
    .col54(shift_register_1_q54), .col55(shift_register_1_q55), .col56(shift_register_1_q56),
    .col57(shift_register_1_q57), .col58(shift_register_1_q58), .col59(shift_register_1_q59),
    .col60(shift_register_1_q60), .col61(shift_register_1_q61), .col62(shift_register_1_q62));
  // RGB_Video #(.cursor("No Cursor"), .height(16), .scale(6), .width(16)) rgb_video_1: pin names not known; wires that end beside it: TRST, CSYNC, CSYNC, ROUT[15:12], ROUT[11:8], ROUT[7:0]
  Bit_Extender #(.in_width(16), .out_width(7)) bit_extender_1 (.in(ROUT), .out(bit_extender_1_out));
  TTY tty_1 (.data(bit_extender_1_out), .clk(CSYNC), .clr(TRST));  // open: we

  // Notes on the sheet:
  //   contents of rom_1 (hex, n*v repeats v):
  //   10c 10d 10e 10e 10f 114 110 10f 111 10e 112 113 48 65 6c 6f 77 72 64 21 20
  //   LOAD 01
  //   JUMP 02
  //   SUM 03
  //   SUB 04
  //   MUL 05
  //   DIV 06
  //   INV 07
  //   AND 08
  //   OR 09
  //   XOR 0a
  //   WRITE 0b
  //   CHANGE 0c
  //   SHR 0d
  //   SHL 0e
endmodule

module RAM_Loader (
  input  [15:0] DROM,
  input  CLK,
  input  RST,
  input  OnNull,
  output [7:0] MC,
  output [15:0] DOUT,
  output SYNC,
  output WE
);

  wire nand_1_out, nor_1_out, not_1_out;

  and and_1 (SYNC, WE, CLK);
  Counter #(.trigger("falling")) counter_1 (.Q(MC), .clk(SYNC), .clr(RST));  // open: load, D, count, carry, up
  assign WE = OnNull ? ~nor_1_out : 1'bz;  // Controlled_Inverter controlled_inverter_1
  nor nor_1 (nor_1_out, DROM[15], DROM[14], DROM[13], DROM[12], DROM[11], DROM[10], DROM[9], DROM[8], DROM[7], DROM[6], DROM[5], DROM[4], DROM[3], DROM[2], DROM[1], DROM[0]);
  assign WE = not_1_out ? nand_1_out : 1'bz;  // Controlled_Buffer controlled_buffer_1
  not not_1 (not_1_out, OnNull);
  nand nand_1 (nand_1_out, MC[7], MC[6], MC[5], MC[4], MC[3], MC[2], MC[1], MC[0]);

  assign DOUT = DROM;
endmodule
